// Logisim project Home Work 5.circ as structural Verilog
module Decode (
  input  [31:0] in_1,
  output [5:0] funct,
  output [4:0] shamt,
  output [4:0] rd,
  output [4:0] rt,
  output [4:0] rs,
  output [15:0] immediate,
  output [25:0] Adress,
  output [5:0] OP
);


  assign Adress = in_1[25:0];
  assign funct = in_1[5:0];
  assign immediate = in_1[15:0];
  assign OP = in_1[31:26];
  assign rd = in_1[15:11];
  assign rs = in_1[25:21];
  assign rt = in_1[20:16];
  assign shamt = in_1[10:6];
endmodule

module addu (
  input  in_1,
  input  in_2,
  input  [3:0] in_3,
  input  in_4,
  input  in_5,
  input  in_6,
  input  in_7,
  input  in_8,
  input  in_9,
  input  in_10,
  output [31:0] out_11
);

  wire alu_1_p4, and_1_out, clock, formadress_1_p2, instructiondecode_1_p1, instructiondecode_1_p5,
       registerfile_1_p6;
  wire [4:0] instructiondecode_1_p2, instructiondecode_1_p3, multiplexer_1_out;
  wire [15:0] instructiondecode_1_p4;
  wire [31:0] adder_1_out, adder_2_out, alu_1_p5, bit_extender_1_out, jumpaddr_1_p3, mips_ram_1_p3,
       multiplexer_2_out, multiplexer_3_out, multiplexer_4_out, register_1_q, registerfile_1_p1,
       registerfile_1_p7, shifter_1_out;

  Clock clock_1 (.out(clock));
  Register #(.width(32)) register_1 (.D(multiplexer_4_out), .Q(register_1_q), .clk(clock), .clr(in_2));  // open: en
  Adder #(.width(32)) adder_1 (.a(32'h4), .b(register_1_q), .out(adder_1_out));  // open: cin, cout
  // MIPSProgramROM mipsprogramrom_1: pin names not known; wires that end beside it: register_1_q, out_11, out_11
  // InstructionDecode instructiondecode_1: pin names not known; wires that end beside it: instructiondecode_1_p1, instructiondecode_1_p2, instructiondecode_1_p3, instructiondecode_1_p4, instructiondecode_1_p5, clock
  Multiplexer #(.width(5), .enable("false")) multiplexer_1 (
    .in0(instructiondecode_1_p2), .in1(instructiondecode_1_p3), .out(multiplexer_1_out), .sel(in_4));
  assign bit_extender_1_out = {{16{1'b0}}, instructiondecode_1_p4};  // Bit_Extender bit_extender_1
  // RegisterFile registerfile_1: pin names not known; wires that end beside it: registerfile_1_p1, in_1, instructiondecode_1_p1, multiplexer_1_out, instructiondecode_1_p2, registerfile_1_p6, registerfile_1_p7
  Multiplexer #(.width(32), .enable("false")) multiplexer_2 (
    .in0(registerfile_1_p7), .in1(bit_extender_1_out), .out(multiplexer_2_out), .sel(in_5));
  Shifter #(.width(32)) shifter_1 (.in(bit_extender_1_out), .\dist (5'b00010), .out(shifter_1_out));
  // ALU alu_1: pin names not known; wires that end beside it: registerfile_1_p6, multiplexer_2_out, in_3, alu_1_p4, alu_1_p5
  Adder #(.width(32)) adder_2 (.a(adder_1_out), .b(shifter_1_out), .out(adder_2_out));  // open: cin, cout
  // JumpAddr jumpaddr_1: pin names not known; wires that end beside it: instructiondecode_1_p5, adder_1_out, jumpaddr_1_p3
  Multiplexer #(.width(32), .enable("false")) multiplexer_3 (
    .in0(adder_1_out), .in1(adder_2_out), .out(multiplexer_3_out), .sel(and_1_out));
  and and_1 (and_1_out, in_9, alu_1_p4);
  // FormAdress formadress_1: pin names not known; wires that end beside it: alu_1_p5, formadress_1_p2, formadress_1_p2, registerfile_1_p7, in_8
  Multiplexer #(.width(32), .enable("false")) multiplexer_4 (
    .in0(multiplexer_3_out), .in1(jumpaddr_1_p3), .out(multiplexer_4_out), .sel(in_10));
  // MIPS_RAM mips_ram_1: pin names not known; wires that end beside it: clock, in_7, mips_ram_1_p3
  Multiplexer #(.width(32), .enable("false")) multiplexer_5 (
    .in0(alu_1_p5), .in1(mips_ram_1_p3), .out(registerfile_1_p1), .sel(in_6));

  // Other names for the same wires on the sheet: ALU_Operation[3:0] = in_3; ALUSrc = in_5; Branch = in_9;
  //   Jump = in_10; MemRead = in_7; MemToReg = in_6; MemWrite = in_8; RegDST = in_4; RegWrite = in_1; reset = in_2
endmodule

module Control_Panel (
  input  Op5,
  input  Op4,
  input  Op3,
  input  Op2,
  input  Op1,
  input  Op0,
  output RegDst,
  output ALUSrc,
  output MemtoReg,
  output RegWrite,
  output MemRead,
  output MemWrite,
  output Branch,
  output ALUOp1,
  output ALUOp0
);

  wire not_2_out, not_3_out, not_4_out, not_5_out, not_6_out;

  not not_1 (RegDst, Op1);
  not not_2 (not_2_out, Op3);
  not not_3 (not_3_out, Op2);
  not not_4 (not_4_out, Op3);
  not not_5 (not_5_out, Op2);
  not not_6 (not_6_out, Op1);
  and and_1 (RegWrite, not_2_out, not_3_out);
  and and_2 (MemRead, not_4_out, Op1);
  and and_3 (ALUOp1, not_5_out, not_6_out);

  assign ALUOp0 = Op2;
  assign ALUSrc = Op1;
  assign Branch = Op2;
  assign MemtoReg = Op1;
  assign MemWrite = Op3;
endmodule
